# Fritzing sketch RFID_Controle_Acesso (saved by Fritzing 0.9.3b)
breadboards: 1

parts:
  Componente1 = RFID-RC522-v2
  Componente2 = Arduino Uno (Rev3)
  LED1 = LED - 5mm [color="Blue (430nm)" package="5 mm [THT]"]
  LED2 = LED - 5mm [color="Red (633nm)" package="5 mm [THT]"]
  LED3 = LED - 5mm [color="Green (555nm)" package="5 mm [THT]"]
  R1 = Resistor [tolerance=±5% resistance=220 package="0402 [SMD]"]
  R2 = Resistor [tolerance=±5% resistance=220 package="0402 [SMD]"]
  R3 = Resistor [tolerance=±5% resistance=220 package="0402 [SMD]"]

nets:
  N1: Componente1.SDA, Componente2.D5_PWM
  N2: Componente1.SCK, Componente2.D4
  N3: Componente1.MOSI, Componente2.D3_PWM
  N4: Componente1.MISO, Componente2.D2
  GND: Componente1.GND, Componente2.GND, LED1.cathode, LED2.cathode, LED3.cathode
  N5: Componente1.RST, Componente2.D6_PWM
  3.3V: Componente1.3.3V, Componente2.3V3
  N6: Componente2.D8, R3.Pin_0
  N7: Componente2.D9_PWM, R2.Pin_0
  N8: Componente2.D10_PWM/SS, R1.Pin_0
  N9: LED1.anode, R3.Pin_1
  N10: LED2.anode, R2.Pin_1
  N11: LED3.anode, R1.Pin_1

custom parts:
  RFID-RC522-v2: A simple China made RFID-RC522 Reader; do check the pin labels, as this is a MFRC522 based clone.

// code stored in the sketch: projeto-Ivair.ino
/*
 * 
 * Criado por Kaique, Luiz, Thiago
 * 
 *  Data 23/10/2023
 * 
 */
 
#include <SPI.h>
#include <MFRC522.h>
 
#define SS_PIN 5
#define RST_PIN 6


MFRC522 mfrc522(SS_PIN, RST_PIN);   // Cria a instancia do MFRC522

void setup() 
{	
	pinMode(7, OUTPUT);
	pinMode(8, OUTPUT);
  pinMode(9, OUTPUT);
  pinMode(10, OUTPUT);
  pinMode(11, INPUT);
  Serial.begin(9600);   // Inicia uma comunicacao serial na velocidade 9600
  SPI.begin();      // Inicia SPI bus
  mfrc522.PCD_Init();   // Inicia MFRC522
}
void loop() 
{
  // Led pra saber se esta em funcionamento
	digitalWrite(8, HIGH);

  //Espera um cartao e reinicia o loop se nao tiver 
  if ( ! mfrc522.PICC_IsNewCardPresent()) 
  {
    return;
  }

  if ( ! mfrc522.PICC_ReadCardSerial() ) // verifica se foi lido algum codigo serial do cartao
  {
    return;
  }
  //Mostra UID no monitor serial
  Serial.print("UID tag :");
  String content= "";
  byte letter;
  for (byte i = 0; i < mfrc522.uid.size; i++) 
  {
     Serial.print(mfrc522.uid.uidByte[i] < 0x10 ? " 0" : " ");
     Serial.print(mfrc522.uid.uidByte[i], HEX);
         
     content.concat(String(mfrc522.uid.uidByte[i] < 0x10 ? " 0" : " "));
     content.concat(String(mfrc522.uid.uidByte[i], HEX));
  }
  Serial.println();
  Serial.print("Mensagem : ");
  content.toUpperCase();
  if (content.substring(1) == "63 8C E5 C7") //Aqui fica o C?digo do cartao em Hexadecimal que sera verificado
  {
		digitalWrite(8, LOW);
    Serial.println("Acesso autorizado");
 
    digitalWrite(10, HIGH);// LED VERDE acende mostrando a liberacao
    delay(3000);
    digitalWrite(10, LOW);
    
    Serial.println();
		digitalWrite(8, HIGH);
  }
 
 else   {
		digitalWrite(8, LOW);
    Serial.println(" Acesso restrito");
    
    digitalWrite(9, HIGH);// LED VERMELHO acende mostrando liberacao
    delay(3000);
    digitalWrite(9, LOW);

		digitalWrite(8, HIGH);
    
  }
}
